# Fritzing sketch Lab8ProgCircuit (saved by Fritzing 0.9.4)
breadboards: 1

parts:
  Part1 = Arduino Uno (Rev3) - ICSP
  U3 = ATTINY45 [package=dip]
  U4 = ATTINY45 [package=dip]
  S1 = Pushbutton [package="[SMD]"]
  S2 = Pushbutton [package="[SMD]"]
  R1 = Resistor [tolerance=±5% resistance=330 package="0805 [SMD]"]
  LED1 = smd LED [color="Red (635nm)" package="0805 [SMD]"]
  LED2 = smd LED [color="Red (635nm)" package="0805 [SMD]"]
  R2 = Resistor [tolerance=±5% resistance=330 package="0805 [SMD]"]
  LED3 = smd LED [color="Green (565nm)" package="0805 [SMD]"]
  R3 = Resistor [tolerance=±5% resistance=220 package="0805 [SMD]"]
  S3 = Pushbutton [package="[SMD]"]

nets:
  N1: Part1.A5/SCL, S3.Pin_3, S3.Pin_4
  VCC: Part1.5V, U3.VCC, U4.VCC
  N2: Part1.D10_PWM/SS, U3.PB5(NRES)
  N3: Part1.D11_PWM/MOSI, U3.PB0(MOSI)
  N4: Part1.D12/MISO, U3.PB1(MISO)
  N5: Part1.D13/SCK, U3.PB2(SCK_ADC1)
  GND: Part1.GND, U3.GND, U4.GND, S1.Pin_1, S1.Pin_2, S2.Pin_3, S2.Pin_4, R1.Pin_1, R2.Pin_1, R3.Pin_0, S3.Pin_1, S3.Pin_2
  N6: Part1.D2, LED3.anode
  N7: U4.PB3(ADC3), S1.Pin_3, S1.Pin_4
  N8: U4.PB4(ADC2), S2.Pin_1, S2.Pin_2
  N9: U4.PB1(MISO), LED2.anode
  N10: U4.PB2(SCK_ADC1), LED1.anode
  N11: R1.Pin_0, LED1.cathode
  N12: LED2.cathode, R2.Pin_0
  N13: LED3.cathode, R3.Pin_1

notes:
  CLK
  T
  Attiny Test Circuit
  Attiny Programmer
  Program
  Status LED<module fritzingVersion="0.9.4.2019-12-01.CD-498-0-a1ffcea">
  <boundingRects>
  <boundingRect name="Breadboard View" rect="445.28 230.321 98.5761 33"/>
  <boundingRect name="Schematic View" rect="0 0 0 0"/>
  <boundingRect name="PCB View" rect="0 0 0 0"/>
  </boundingRects>
  <instances>
  <instance path=":/resources/parts/core/note.fzp" moduleIdRef="NoteModuleID" modelIndex="85578920">
  <title>Note2</title>
  <text>&lt;!DOCTYPE HTML PUBLIC "-//W3C//DTD HTML 4.0//EN" "http://www.w3.org/TR/REC-html40/strict.dtd">&#xd;
  &lt;html>&lt;head>&lt;meta name="qrichtext" content="1" />&lt;style type="text/css">&#xd;
  p, li { white-space: pre-wrap; }&#xd;
  &lt;/style>&lt;/head>&lt;body style=" font-family:'Droid Sans'; font-size:9pt; font-weight:400; font-style:normal;">&#xd;
  &lt;p style=" margin-top:0px; margin-bottom:0px; margin-left:0px; margin-right:0px; -qt-block-indent:0; text-indent:0px;">Attiny Programmer&lt;/p>&lt;/body>&lt;/html></text>
  <views>
  <breadboardView layer="breadboardNote">
  <geometry width="98.5761" y="230.321" height="33" x="445.28" z="6.50003"/>
  </breadboardView>
  </views>
  </instance>
  </instances>
  </module>
  Program Btn
  Dime
  Quarter
